// Logisim project stage3.circ as structural Verilog: 3 circuits, main circuit main
module main (
  input  in_1
);

  wire button_1_out, button_3_out, clock_1_out, firstdigitsecond_1__9sec, j_k_ff_1_q;
  wire [2:0] seconddigitsecond_1_out_5;
  wire [3:0] firstdigitsecond_1_out0;

  Button button_1 (.out(button_1_out));
  J_K_Flip_Flop j_k_ff_1 (
    .J(button_1_out), .K(button_1_out), .clk(button_1_out), .Q(j_k_ff_1_q));  // open: Qn, preset, reset
  Clock clock_1 (.out(clock_1_out));
  Button button_2 ();  // open: out
  Button button_3 (.out(button_3_out));
  LED led_1 (.in(j_k_ff_1_q));
  FirstDigitSecond firstdigitsecond_1 (
    .Reset(button_3_out), .JK(j_k_ff_1_q), .clock(clock_1_out), .Out3(firstdigitsecond_1_out0[3]),
    ._9sec(firstdigitsecond_1__9sec), .Out0(firstdigitsecond_1_out0[0]), .Out1(firstdigitsecond_1_out0[1]),
    .Out2(firstdigitsecond_1_out0[2]));
  Hex_Digit_Display hex_digit_display_1 ();  // open: value, dp
  Hex_Digit_Display hex_digit_display_2 ();  // open: value, dp
  Hex_Digit_Display hex_digit_display_3 (.value({in_1, seconddigitsecond_1_out_5}));  // open: dp
  Hex_Digit_Display hex_digit_display_4 (.value(firstdigitsecond_1_out0));  // open: dp
  SecondDigitSecond seconddigitsecond_1 (
    .reset(button_3_out), ._5sec(firstdigitsecond_1__9sec), .CLK(clock_1_out),
    .out_5(seconddigitsecond_1_out_5[0]), .out_6(seconddigitsecond_1_out_5[1]),
    .out_7(seconddigitsecond_1_out_5[2]));  // open: _5sec_2
  Hex_Digit_Display hex_digit_display_5 ();  // open: value, dp
  Hex_Digit_Display hex_digit_display_6 ();  // open: value, dp
  Hex_Digit_Display hex_digit_display_7 ();  // open: value, dp
  Hex_Digit_Display hex_digit_display_8 ();  // open: value, dp

  // Notes on the sheet:
  //   Start / Stop
  //   Stopwatch Interface
  //   Split
  //   Reset
  //   Clock Started
  //   Elapsed Time
  //   Minutes
  //   :
  //   Seconds
  //   Split Time
  //   Minutes
  //   :
  //   Seconds
endmodule

module FirstDigitSecond (
  input  Reset,
  input  JK,
  input  clock,
  output _9sec,
  output Out0,
  output Out1,
  output Out2,
  output Out3
);

  wire and_1_out, and_2_out, and_3_out, j_k_ff_1_q, j_k_ff_2_q, j_k_ff_3_q, j_k_ff_4_q, or_1_out;

  J_K_Flip_Flop j_k_ff_1 (.J(JK), .K(JK), .clk(clock), .Q(j_k_ff_1_q), .reset(or_1_out));  // open: Qn, preset
  D_Flip_Flop d_ff_1 (.D(j_k_ff_1_q), .clk(clock), .Q(Out0));  // open: Qn, preset, reset
  J_K_Flip_Flop j_k_ff_2 (
    .J(j_k_ff_1_q), .K(j_k_ff_1_q), .clk(clock), .Q(j_k_ff_2_q), .reset(or_1_out));  // open: Qn, preset
  and and_1 (and_1_out, j_k_ff_1_q, j_k_ff_2_q);
  D_Flip_Flop d_ff_2 (.D(j_k_ff_2_q), .clk(clock), .Q(Out1));  // open: Qn, preset, reset
  J_K_Flip_Flop j_k_ff_3 (
    .J(and_1_out), .K(and_1_out), .clk(clock), .Q(j_k_ff_3_q), .reset(or_1_out));  // open: Qn, preset
  D_Flip_Flop d_ff_3 (.D(j_k_ff_3_q), .clk(clock), .Q(Out2));  // open: Qn, preset, reset
  and and_2 (and_2_out, and_1_out, j_k_ff_3_q);
  J_K_Flip_Flop j_k_ff_4 (
    .J(and_2_out), .K(and_2_out), .clk(clock), .Q(j_k_ff_4_q), .reset(or_1_out));  // open: Qn, preset
  D_Flip_Flop d_ff_4 (.D(j_k_ff_4_q), .clk(clock), .Q(Out3));  // open: Qn, preset, reset
  or or_1 (or_1_out, Reset, and_3_out);
  and and_3 (and_3_out, j_k_ff_2_q, j_k_ff_4_q);
  and and_4 (_9sec, j_k_ff_4_q, j_k_ff_1_q);
endmodule

module SecondDigitSecond (
  input  reset,
  input  _5sec,
  input  CLK,
  output _5sec_2,
  output out_5,
  output out_6,
  output out_7
);

  wire and_1_out, and_2_out, and_3_out, j_k_ff_1_q, j_k_ff_2_q, j_k_ff_3_q, or_1_out;

  J_K_Flip_Flop j_k_ff_1 (.J(_5sec), .K(_5sec), .clk(CLK), .Q(j_k_ff_1_q), .reset(or_1_out));  // open: Qn, preset
  D_Flip_Flop d_ff_1 (.D(j_k_ff_1_q), .clk(CLK), .Q(out_5));  // open: Qn, preset, reset
  and and_1 (and_1_out, _5sec, j_k_ff_1_q);
  J_K_Flip_Flop j_k_ff_2 (
    .J(and_1_out), .K(and_1_out), .clk(CLK), .Q(j_k_ff_2_q), .reset(or_1_out));  // open: Qn, preset
  and and_2 (and_2_out, and_1_out, j_k_ff_2_q);
  D_Flip_Flop d_ff_2 (.D(j_k_ff_2_q), .clk(CLK), .Q(out_6));  // open: Qn, preset, reset
  J_K_Flip_Flop j_k_ff_3 (
    .J(and_2_out), .K(and_2_out), .clk(CLK), .Q(j_k_ff_3_q), .reset(or_1_out));  // open: Qn, preset
  and and_3 (and_3_out, j_k_ff_2_q, j_k_ff_3_q);
  D_Flip_Flop d_ff_3 (.D(j_k_ff_3_q), .clk(CLK), .Q(out_7));  // open: Qn, preset, reset
  or or_1 (or_1_out, reset, and_3_out);
  and and_4 (_5sec_2, j_k_ff_3_q, j_k_ff_1_q);
endmodule
