// Logisim project stage4.circ as structural Verilog: 5 circuits, main circuit main
module main (
  input  in_1
);

  wire button_1_out, button_3_out, clock_1_out, firstdigitminute_1__9min, firstdigitsecond_1__5sec,
       j_k_ff_1_q, seconddigitsecond_1__9sec;
  wire [2:0] seconddigitsecond_1_out0;
  wire [3:0] firstdigitminute_1_out0, firstdigitsecond_1_out0, seconddigitmintute_1_out0;

  Button button_1 (.out(button_1_out));
  J_K_Flip_Flop j_k_ff_1 (
    .J(button_1_out), .K(button_1_out), .clk(button_1_out), .Q(j_k_ff_1_q));  // open: Qn, preset, reset
  Clock clock_1 (.out(clock_1_out));
  Button button_2 ();  // open: out
  Button button_3 (.out(button_3_out));
  LED led_1 (.in(j_k_ff_1_q));
  FirstDigitSecond firstdigitsecond_1 (
    .Reset(button_3_out), .JK(j_k_ff_1_q), .clock(clock_1_out), .Out3(firstdigitsecond_1_out0[3]),
    ._5sec(firstdigitsecond_1__5sec), .Out0(firstdigitsecond_1_out0[0]), .Out1(firstdigitsecond_1_out0[1]),
    .Out2(firstdigitsecond_1_out0[2]));
  Hex_Digit_Display hex_digit_display_1 (.value(seconddigitmintute_1_out0));  // open: dp
  SecondDigitSecond seconddigitsecond_1 (
    .reset(button_3_out), ._5sec(firstdigitsecond_1__5sec), .CLK(clock_1_out),
    ._9sec(seconddigitsecond_1__9sec), .Out0(seconddigitsecond_1_out0[0]),
    .Out1(seconddigitsecond_1_out0[1]), .Out2(seconddigitsecond_1_out0[2]));
  FirstDigitMinute firstdigitminute_1 (
    .Reset(button_3_out), ._9sec(firstdigitsecond_1__5sec), ._5sec(seconddigitsecond_1__9sec),
    .CLK(clock_1_out), .Out3(firstdigitminute_1_out0[3]), ._9min(firstdigitminute_1__9min),
    .Out0(firstdigitminute_1_out0[0]), .Out1(firstdigitminute_1_out0[1]), .Out2(firstdigitminute_1_out0[2]));
  Hex_Digit_Display hex_digit_display_2 (.value(firstdigitminute_1_out0));  // open: dp
  Hex_Digit_Display hex_digit_display_3 (.value({in_1, seconddigitsecond_1_out0}));  // open: dp
  Hex_Digit_Display hex_digit_display_4 (.value(firstdigitsecond_1_out0));  // open: dp
  SecondDigitMintute seconddigitmintute_1 (
    .Reset(button_3_out), ._9sec(firstdigitsecond_1__5sec), ._5sec(seconddigitsecond_1__9sec),
    ._9min(firstdigitminute_1__9min), .CLK(clock_1_out), .out_9(seconddigitmintute_1_out0[3]),
    .Out0(seconddigitmintute_1_out0[0]), .Out1(seconddigitmintute_1_out0[1]),
    .out_8(seconddigitmintute_1_out0[2]));
  Hex_Digit_Display hex_digit_display_5 ();  // open: value, dp
  Hex_Digit_Display hex_digit_display_6 ();  // open: value, dp
  Hex_Digit_Display hex_digit_display_7 ();  // open: value, dp
  Hex_Digit_Display hex_digit_display_8 ();  // open: value, dp

  // Notes on the sheet:
  //   Start / Stop
  //   Split
  //   Stopwatch Interface
  //   Reset
  //   Clock Started
  //   Minutes
  //   Elapsed Time
  //   :
  //   Seconds
  //   Minutes
  //   Split Time
  //   :
  //   Seconds
endmodule

module FirstDigitSecond (
  input  Reset,
  input  JK,
  input  clock,
  output _5sec,
  output Out0,
  output Out1,
  output Out2,
  output Out3
);

  wire and_1_out, and_2_out, and_3_out, j_k_ff_1_q, j_k_ff_2_q, j_k_ff_3_q, j_k_ff_4_q, or_1_out;

  J_K_Flip_Flop j_k_ff_1 (.J(JK), .K(JK), .clk(clock), .Q(j_k_ff_1_q), .reset(or_1_out));  // open: Qn, preset
  D_Flip_Flop d_ff_1 (.D(j_k_ff_1_q), .clk(clock), .Q(Out0));  // open: Qn, preset, reset
  J_K_Flip_Flop j_k_ff_2 (
    .J(j_k_ff_1_q), .K(j_k_ff_1_q), .clk(clock), .Q(j_k_ff_2_q), .reset(or_1_out));  // open: Qn, preset
  and and_1 (and_1_out, j_k_ff_1_q, j_k_ff_2_q);
  D_Flip_Flop d_ff_2 (.D(j_k_ff_2_q), .clk(clock), .Q(Out1));  // open: Qn, preset, reset
  J_K_Flip_Flop j_k_ff_3 (
    .J(and_1_out), .K(and_1_out), .clk(clock), .Q(j_k_ff_3_q), .reset(or_1_out));  // open: Qn, preset
  D_Flip_Flop d_ff_3 (.D(j_k_ff_3_q), .clk(clock), .Q(Out2));  // open: Qn, preset, reset
  and and_2 (and_2_out, and_1_out, j_k_ff_3_q);
  J_K_Flip_Flop j_k_ff_4 (
    .J(and_2_out), .K(and_2_out), .clk(clock), .Q(j_k_ff_4_q), .reset(or_1_out));  // open: Qn, preset
  D_Flip_Flop d_ff_4 (.D(j_k_ff_4_q), .clk(clock), .Q(Out3));  // open: Qn, preset, reset
  or or_1 (or_1_out, Reset, and_3_out);
  and and_3 (and_3_out, j_k_ff_2_q, j_k_ff_4_q);
  and and_4 (_5sec, j_k_ff_4_q, j_k_ff_1_q);
endmodule

module SecondDigitSecond (
  input  reset,
  input  _5sec,
  input  CLK,
  output _9sec,
  output Out0,
  output Out1,
  output Out2
);

  wire and_1_out, and_2_out, and_3_out, j_k_ff_1_q, j_k_ff_2_q, j_k_ff_3_q, or_1_out;

  J_K_Flip_Flop j_k_ff_1 (.J(_5sec), .K(_5sec), .clk(CLK), .Q(j_k_ff_1_q), .reset(or_1_out));  // open: Qn, preset
  D_Flip_Flop d_ff_1 (.D(j_k_ff_1_q), .clk(CLK), .Q(Out0));  // open: Qn, preset, reset
  and and_1 (and_1_out, _5sec, j_k_ff_1_q);
  J_K_Flip_Flop j_k_ff_2 (
    .J(and_1_out), .K(and_1_out), .clk(CLK), .Q(j_k_ff_2_q), .reset(or_1_out));  // open: Qn, preset
  and and_2 (and_2_out, and_1_out, j_k_ff_2_q);
  D_Flip_Flop d_ff_2 (.D(j_k_ff_2_q), .clk(CLK), .Q(Out1));  // open: Qn, preset, reset
  J_K_Flip_Flop j_k_ff_3 (
    .J(and_2_out), .K(and_2_out), .clk(CLK), .Q(j_k_ff_3_q), .reset(or_1_out));  // open: Qn, preset
  and and_3 (and_3_out, j_k_ff_2_q, j_k_ff_3_q);
  D_Flip_Flop d_ff_3 (.D(j_k_ff_3_q), .clk(CLK), .Q(Out2));  // open: Qn, preset, reset
  or or_1 (or_1_out, reset, and_3_out);
  and and_4 (_9sec, j_k_ff_3_q, j_k_ff_1_q);
endmodule

module FirstDigitMinute (
  input  Reset,
  input  _9sec,
  input  _5sec,
  input  CLK,
  output _9min,
  output Out0,
  output Out1,
  output Out2,
  output Out3
);

  wire and_1_out, and_2_out, and_3_out, and_4_out, and_5_out, j_k_ff_1_q, j_k_ff_2_q, j_k_ff_3_q, j_k_ff_4_q,
       or_1_out;

  and and_1 (and_1_out, _9sec, _5sec);
  J_K_Flip_Flop j_k_ff_1 (
    .J(and_1_out), .K(and_1_out), .clk(CLK), .Q(j_k_ff_1_q), .reset(or_1_out));  // open: Qn, preset
  and and_2 (and_2_out, and_1_out, j_k_ff_1_q);
  D_Flip_Flop d_ff_1 (.D(j_k_ff_1_q), .clk(CLK), .Q(Out0));  // open: Qn, preset, reset
  J_K_Flip_Flop j_k_ff_2 (
    .J(and_2_out), .K(and_2_out), .clk(CLK), .Q(j_k_ff_2_q), .reset(or_1_out));  // open: Qn, preset
  and and_3 (and_3_out, and_2_out, j_k_ff_2_q);
  D_Flip_Flop d_ff_2 (.D(j_k_ff_2_q), .clk(CLK), .Q(Out1));  // open: Qn, preset, reset
  J_K_Flip_Flop j_k_ff_3 (
    .J(and_3_out), .K(and_3_out), .clk(CLK), .Q(j_k_ff_3_q), .reset(or_1_out));  // open: Qn, preset
  D_Flip_Flop d_ff_3 (.D(j_k_ff_3_q), .clk(CLK), .Q(Out2));  // open: Qn, preset, reset
  and and_4 (and_4_out, and_3_out, j_k_ff_3_q);
  J_K_Flip_Flop j_k_ff_4 (
    .J(and_4_out), .K(and_4_out), .clk(CLK), .Q(j_k_ff_4_q), .reset(or_1_out));  // open: Qn, preset
  D_Flip_Flop d_ff_4 (.D(j_k_ff_4_q), .clk(CLK), .Q(Out3));  // open: Qn, preset, reset
  and and_5 (and_5_out, j_k_ff_2_q, j_k_ff_4_q);
  or or_1 (or_1_out, Reset, and_5_out);
  and and_6 (_9min, j_k_ff_4_q, j_k_ff_1_q);
endmodule

module SecondDigitMintute (
  input  Reset,
  input  _9sec,
  input  _5sec,
  input  _9min,
  input  CLK,
  output Out0,
  output Out1,
  output out_8,
  output out_9
);

  wire and_1_out, and_2_out, and_3_out, and_4_out, and_5_out, j_k_ff_1_q, j_k_ff_2_q, j_k_ff_3_q, j_k_ff_4_q,
       or_1_out;

  and and_1 (and_1_out, _9sec, _5sec, _9min);
  J_K_Flip_Flop j_k_ff_1 (
    .J(and_1_out), .K(and_1_out), .clk(CLK), .Q(j_k_ff_1_q), .reset(or_1_out));  // open: Qn, preset
  and and_2 (and_2_out, and_1_out, j_k_ff_1_q);
  D_Flip_Flop d_ff_1 (.D(j_k_ff_1_q), .clk(CLK), .Q(Out0));  // open: Qn, preset, reset
  J_K_Flip_Flop j_k_ff_2 (
    .J(and_2_out), .K(and_2_out), .clk(CLK), .Q(j_k_ff_2_q), .reset(or_1_out));  // open: Qn, preset
  and and_3 (and_3_out, and_2_out, j_k_ff_2_q);
  D_Flip_Flop d_ff_2 (.D(j_k_ff_2_q), .clk(CLK), .Q(Out1));  // open: Qn, preset, reset
  J_K_Flip_Flop j_k_ff_3 (
    .J(and_3_out), .K(and_3_out), .clk(CLK), .Q(j_k_ff_3_q), .reset(or_1_out));  // open: Qn, preset
  D_Flip_Flop d_ff_3 (.D(j_k_ff_3_q), .clk(CLK), .Q(out_8));  // open: Qn, preset, reset
  and and_4 (and_4_out, and_3_out, j_k_ff_3_q);
  J_K_Flip_Flop j_k_ff_4 (
    .J(and_4_out), .K(and_4_out), .clk(CLK), .Q(j_k_ff_4_q), .reset(or_1_out));  // open: Qn, preset
  D_Flip_Flop d_ff_4 (.D(j_k_ff_4_q), .clk(CLK), .Q(out_9));  // open: Qn, preset, reset
  and and_5 (and_5_out, j_k_ff_2_q, j_k_ff_4_q);
  or or_1 (or_1_out, Reset, and_5_out);

  // Notes on the sheet:
  //   Out2
  //   Out3
endmodule
